# Fritzing sketch ArduinoFab_WK5_pressInput (saved by Fritzing 0.9.3b)
breadboards: 1

parts:
  元件1 = Arduino Uno (Rev3)
  元件2 = OLED Monochrome 128x64 0.96 inch [part_number=326]
  R1 = Resistor [tolerance=±5% resistance=220 package=THT]
  J1 = Basic Force Sensing Resistor (FSR) [package=THT]
  D1 = LED_BARGRAPH_10 [package=led_bargaph_10]
  R2 = Resistor [tolerance=±5% resistance=220 package=THT]
  R3 = Resistor [tolerance=±5% resistance=220 package=THT]
  R4 = Resistor [tolerance=±5% resistance=220 package=THT]
  R5 = Resistor [tolerance=±5% resistance=220 package=THT]
  R6 = Resistor [tolerance=±5% resistance=220 package=THT]
  R7 = Resistor [tolerance=±5% resistance=220 package=THT]
  R8 = Resistor [tolerance=±5% resistance=220 package=THT]
  R9 = Resistor [tolerance=±5% resistance=220 package=THT]
  R10 = Resistor [tolerance=±5% resistance=220 package=THT]
  R11 = Resistor [tolerance=±5% resistance=220 package=THT]

nets:
  N1: 元件1.A0, R1.Pin_0, J1.pin_0
  N2: 元件1.A3, D1.A_C
  N3: 元件1.A4/SDA, D1.B_C
  N4: 元件1.D8, 元件2.3.3V
  N5: 元件1.D9_PWM, 元件2.CS
  N6: 元件1.D10_PWM/SS, 元件2.RESET
  N7: 元件1.D11_PWM/MOSI, 元件2.DC_SA0
  N8: 元件1.D12/MISO, 元件2.SCLK_SCK
  N9: 元件1.D13/SCK, 元件2.MOSI_SDA
  N10: 元件1.D0/RX, D1.J_C
  N11: 元件1.D1/TX, D1.I_C
  N12: 元件1.D2, D1.H_C
  N13: 元件1.D3_PWM, D1.G_C
  N14: 元件1.D4, D1.F_C
  N15: 元件1.D5_PWM, D1.E_C
  N16: 元件1.D6_PWM, D1.D_C
  N17: 元件1.D7, D1.C_C
  5V: 元件1.5V, 元件2.VIN, R1.Pin_1, J1.pin_1
  GND: 元件1.GND, 元件2.GND, R2.Pin_1, R3.Pin_1, R4.Pin_1, R5.Pin_1, R6.Pin_1, R7.Pin_1, R8.Pin_1, R9.Pin_1, R10.Pin_1, R11.Pin_1
  N18: D1.A_A, R2.Pin_0
  N19: D1.B_A, R3.Pin_0
  N20: D1.C_A, R4.Pin_0
  N21: D1.D_A, R5.Pin_0
  N22: D1.E_A, R6.Pin_0
  N23: D1.F_A, R7.Pin_0
  N24: D1.G_A, R8.Pin_0
  N25: D1.H_A, R9.Pin_0
  N26: D1.I_A, R10.Pin_0
  N27: D1.J_A, R11.Pin_0

custom parts:
  OLED Monochrome 128x64 0.96 inch: These displays are small, only about 1" diameter, but very readable due to the high contrast of an OLED display. This display is made of 128x64 individual white OLED pixels, each one is turned on or off by the controller chip. Because the display makes its own light, no backlight is required. This reduces the power required to run the OLED and is why the display has such high contrast; we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
